# Fritzing sketch MotorControlSchematic (saved by Fritzing 0.9.2b)
breadboards: 1

parts:
  Part1 = Photon
  Q1 = npn-Powertransistor [part_number=TIP31C package="TO220 [THT]"]
  R1 = Resistor [tolerance=±5% resistance=330 package="0603 [SMD]"]
  M1 = DC Motor
  V1 = DC Power [voltage=5]
  D1 = Rectifier Diode [part_number=1N4001 package="300 mil [THT]"]
  RHT1 = Humidity and Temperature Sensor RHT03 [part_number=DHT22]
  R2 = Resistor [tolerance=±5% resistance=1k package="1206 [SMD]"]

nets:
  N1: Part1.GND, Q1.emitter, V1.V-, RHT1.GND_2
  N2: Part1.VIN, M1.pin_1, V1.V+, D1.cathode
  N3: Part1.D1, R1.Pin_0
  N4: Part1.D2, RHT1.Data-signal, R2.Pin_1
  3V3: Part1.3V3, RHT1.Vcc, R2.Pin_0
  N5: Q1.base, R1.Pin_1
  N6: Q1.collector, M1.pin_2, D1.anode

notes:
  WIRE LEGEND
  White - Ground
  Red- +5V
  Purple - +3.3V
  Blue- Circuit wires
